// Logisim project faerie.circ as structural Verilog: 3 circuits, main circuit main
module main (
);

  wire alu_1_cout, and_1_out, and_2_out, and_3_out, and_4_out, and_5_out, and_6_out, and_7_out, button_1_out,
       CF_q, clock_1_out, comparator_1_eq, control_unit_1_async_reset_b, control_unit_1_branch,
       control_unit_1_increment_al, control_unit_1_memory_read, control_unit_1_memory_write,
       control_unit_1_pc_as_address, control_unit_1_set_ah, control_unit_1_set_al, control_unit_1_write_a,
       control_unit_1_write_fr, control_unit_1_zero_page_address, multiplexer_2_out, not_1_out, or_2_out,
       or_3_out, xor_3_out, ZF_q;
  wire [0:0] AL_q;
  wire [3:0] control_unit_1_mode_select;
  wire [7:0] A_q, AH_q, alu_1_q, B_q, bit_extender_1_out, controlled_buffer_1_out;
  wire [13:0] bit_extender_2_out;
  wire [14:0] bit_extender_3_out;
  wire [15:0] multiplexer_1_out, or_1_out, PC_q, xor_1_out, xor_2_out;

  assign bit_extender_1_out = {{7{control_unit_1_zero_page_address}}, control_unit_1_zero_page_address};  // Bit_Extender bit_extender_1
  and and_1 (and_1_out, or_3_out, control_unit_1_branch);
  assign xor_1_out = 16'hc000 ^ or_1_out;  // XOR_Gate xor_1, 16 bits wide
  assign xor_2_out = 16'hc000 ^ PC_q;  // XOR_Gate xor_2, 16 bits wide
  Counter #(.width(16), .max('hffff)) PC (
    .load(and_1_out), .D(xor_1_out), .count(control_unit_1_pc_as_address), .Q(PC_q), .clk(clock_1_out),
    .clr(button_1_out));  // open: carry
  Register AH (.D(controlled_buffer_1_out), .en(control_unit_1_set_ah), .Q(AH_q), .clk(clock_1_out));  // open: clr
  assign or_1_out[15:8] = ~(~AH_q | bit_extender_1_out);  // NOR_Gate nor_1, 8 bits wide
  or or_1 (or_1_out[0], control_unit_1_increment_al, AL_q[0]);
  Register AL (
    .D(controlled_buffer_1_out), .en(control_unit_1_set_al), .Q({or_1_out[7:1], AL_q[0]}), .clk(clock_1_out));  // open: clr
  control_unit control_unit_1 (
    .Data_bus(controlled_buffer_1_out), .Mode_select(control_unit_1_mode_select),
    .Memory_write(control_unit_1_memory_write), .Memory_read(control_unit_1_memory_read),
    .Branch(control_unit_1_branch), .PC_as_address(control_unit_1_pc_as_address),
    .Set_AL(control_unit_1_set_al), .Set_AH(control_unit_1_set_ah),
    .Zero_page_address(control_unit_1_zero_page_address), .Clock(clock_1_out), .Reset(button_1_out),
    .Async_reset_B(control_unit_1_async_reset_b), .Write_FR(control_unit_1_write_fr),
    .Write_A(control_unit_1_write_a), .Increment_AL(control_unit_1_increment_al));
  Multiplexer #(.width(16), .enable("false")) multiplexer_1 (
    .in0(or_1_out), .in1(xor_2_out), .out(multiplexer_1_out), .sel(control_unit_1_pc_as_address));
  // Probe on multiplexer_1_out
  // Probe on controlled_buffer_1_out
  Button button_1 (.out(button_1_out));
  Clock clock_1 (.out(clock_1_out));
  assign controlled_buffer_1_out = control_unit_1_memory_write ? A_q : 8'bz;  // Controlled_Buffer controlled_buffer_1
  Bit_Extender #(.in_width(16), .out_width(14)) bit_extender_2 (.in(multiplexer_1_out), .out(bit_extender_2_out));
  and and_2 (and_2_out, control_unit_1_memory_read, multiplexer_1_out[14], multiplexer_1_out[15]);
  Bit_Extender #(.in_width(16), .out_width(15)) bit_extender_3 (.in(multiplexer_1_out), .out(bit_extender_3_out));
  not not_1 (not_1_out, multiplexer_1_out[15]);
  LED led_1 (.in(control_unit_1_memory_read));
  LED led_2 (.in(control_unit_1_memory_write));
  Register A (.D(alu_1_q), .en(control_unit_1_write_a), .Q(A_q), .clk(clock_1_out), .clr(button_1_out));
  ALU alu_1 (
    .Cin(CF_q), .A(A_q), .B(B_q), .Cout(alu_1_cout), .Q(alu_1_q), .CC(control_unit_1_mode_select[3]),
    .SUB_AND(control_unit_1_mode_select[2]), .SHL_XOR(control_unit_1_mode_select[1]),
    .LOGIC_B(control_unit_1_mode_select[0]));
  Register B (
    .D(controlled_buffer_1_out), .en(control_unit_1_memory_read), .Q(B_q), .clk(clock_1_out),
    .clr(control_unit_1_async_reset_b));
  and and_3 (and_3_out, not_1_out, control_unit_1_memory_read);
  and and_4 (and_4_out, not_1_out, control_unit_1_memory_write);
  Register #(.width(1)) CF (
    .D(alu_1_cout), .en(control_unit_1_write_fr), .Q(CF_q), .clk(clock_1_out), .clr(button_1_out));
  and and_5 (and_5_out, CF_q, ~ZF_q);  // AND_Gate
  and and_6 (and_6_out, ~ZF_q, ~CF_q);  // AND_Gate
  ROM #(.addrWidth(14)) rom_1 (.addr(bit_extender_2_out), .data(controlled_buffer_1_out), .sel(and_2_out));
  RAM #(.addrWidth(15), .bus("separate")) ram_1 (
    .addr(bit_extender_3_out), .din(controlled_buffer_1_out), .data(controlled_buffer_1_out),
    .str(and_4_out), .clk(clock_1_out), .ld(and_3_out));  // open: sel, clr
  or or_2 (or_2_out, ~control_unit_1_mode_select[3], ZF_q);  // OR_Gate
  Comparator comparator_1 (.a(alu_1_q), .b({8{1'b0}}), .eq(comparator_1_eq));  // open: gt, lt
  Multiplexer #(.select(2), .enable("false")) multiplexer_2 (
    .in0(ZF_q), .in1(CF_q), .in2(and_5_out), .in3(and_6_out), .out(multiplexer_2_out),
    .sel(control_unit_1_mode_select[1:0]));
  and and_7 (and_7_out, or_2_out, comparator_1_eq);
  Register #(.width(1)) ZF (
    .D(and_7_out), .en(control_unit_1_write_fr), .Q(ZF_q), .clk(clock_1_out), .clr(button_1_out));
  xor xor_3 (xor_3_out, multiplexer_2_out, control_unit_1_mode_select[2]);
  or or_3 (or_3_out, xor_3_out, control_unit_1_mode_select[3]);

  // Notes on the sheet:
  //   contents of rom_1 (hex, n*v repeats v):
  //   5c 0 2 0 2 2 5c 1 2 1 50 0 20 1 1b 0 c0 2 2 50 0 2 1 50 2 2 0 8b a c0
endmodule

module control_unit (
  input  [7:0] Data_bus,
  input  Clock,
  input  Reset,
  output Memory_write,
  output Memory_read,
  output Branch,
  output PC_as_address,
  output Set_AL,
  output Set_AH,
  output Zero_page_address,
  output Async_reset_B,
  output Write_FR,
  output Write_A,
  output Increment_AL,
  output [3:0] Mode_select
);

  wire and_2_out, demultiplexer_1_out0, demultiplexer_2_out0, demultiplexer_3_out0, demultiplexer_4_out0,
       demultiplexer_4_out1, demultiplexer_5_out1, nand_1_out, nor_1_out, nor_2_out, nor_3_out, not_1_out,
       or_1_out, or_2_out, or_5_out;
  wire [3:0] multiplexer_1_out;
  wire [4:0] FSM_q;
  wire [7:0] demultiplexer_2_out1, IR_q;

  and and_1 (Async_reset_B, Clock, nor_1_out);
  not not_1 (not_1_out, nor_1_out);
  Register IR (.D(Data_bus), .en(nor_1_out), .Q(IR_q), .clk(Clock), .clr(Reset));
  Multiplexer #(.width(8), .enable("false")) multiplexer_1 (
    .in0(Data_bus), .in1(IR_q), .out({Mode_select, multiplexer_1_out}), .sel(not_1_out));
  nor nor_1 (nor_1_out, FSM_q[0], FSM_q[1], Increment_AL, FSM_q[3], FSM_q[4], Write_FR, Memory_write, Branch);
  Register FSM (
    .D({demultiplexer_2_out1[7:4], Increment_AL, demultiplexer_2_out1[2:0]}),
    .Q({Branch, Memory_write, Write_FR, FSM_q[4:3], Increment_AL, FSM_q[1:0]}), .clk(Clock), .clr(Reset));  // open: en
  nor nor_2 (nor_2_out, Mode_select[0], Mode_select[1]);
  or or_1 (or_1_out, nor_1_out, FSM_q[0], FSM_q[1]);
  or or_2 (or_2_out, Increment_AL, FSM_q[3], FSM_q[4]);
  or or_3 (Memory_read, or_1_out, or_2_out);
  Demultiplexer #(.enable("false")) demultiplexer_1 (
    .out0(demultiplexer_1_out0), .out1(demultiplexer_2_out1[1]), .in(FSM_q[0]), .sel(multiplexer_1_out[3]));
  or or_4 (PC_as_address, or_1_out, and_2_out);
  and and_2 (and_2_out, FSM_q[4], ~nand_1_out);  // AND_Gate
  Demultiplexer #(.enable("false")) demultiplexer_2 (
    .out0(demultiplexer_2_out0), .out1(demultiplexer_2_out1[0]), .in(nor_1_out), .sel(nand_1_out));
  Demultiplexer #(.enable("false")) demultiplexer_3 (
    .out0(demultiplexer_3_out0), .out1(demultiplexer_2_out1[2]), .in(demultiplexer_1_out0),
    .sel(multiplexer_1_out[2]));
  nand nand_1 (nand_1_out, multiplexer_1_out[2], multiplexer_1_out[3]);
  or or_5 (or_5_out, demultiplexer_2_out0, demultiplexer_3_out0, FSM_q[1], FSM_q[3]);
  Demultiplexer #(.enable("false")) demultiplexer_4 (
    .out0(demultiplexer_4_out0), .out1(demultiplexer_4_out1), .in(or_5_out), .sel(multiplexer_1_out[1]));
  nor nor_3 (nor_3_out, multiplexer_1_out[3], multiplexer_1_out[2]);
  Demultiplexer #(.enable("false")) demultiplexer_5 (
    .out0(demultiplexer_2_out1[4]), .out1(demultiplexer_5_out1), .in(demultiplexer_4_out0), .sel(nor_2_out));
  Demultiplexer #(.enable("false")) demultiplexer_6 (
    .out0(demultiplexer_2_out1[6]), .out1(demultiplexer_2_out1[7]), .in(demultiplexer_4_out1),
    .sel(multiplexer_1_out[0]));
  or or_6 (Set_AL, FSM_q[0], FSM_q[3]);
  or or_7 (Set_AH, FSM_q[1], Increment_AL);
  or or_8 (Zero_page_address, FSM_q[3], nor_3_out, Increment_AL);
  and and_3 (Write_A, Write_FR, ~multiplexer_1_out[0]);  // AND_Gate
  or or_9 (demultiplexer_2_out1[5], demultiplexer_5_out1, FSM_q[4]);

  // Notes on the sheet:
  //   Reset: pull=down
  //   Branch: pull=down
  //   Mode_select: pull=down
  //   Set_AL: pull=down
  //   Clock: pull=down
  //   Zero_page_address: pull=down
  //   Set_AH: pull=down
  //   Memory_read: pull=down
  //   Data_bus: pull=down
  //   Memory_write: pull=down
  //   PC_as_address: pull=down
  //   Insn load
  //   Addr #1
  //   Addr #2
  //   Ptr #1
  //   Ptr #2
  //   Mem load
  //   ALU
  //   Mem store
  //   Branch
  //   Addr #1
  //   Addr #2
  //   Ptr #1
  //   Ptr #2
  //   Mem load
  //   ALU
  //   Mem store
  //   Branch
endmodule

module ALU (
  input  CC,
  input  Cin,
  input  [7:0] A,
  input  [7:0] B,
  input  SUB_AND,
  input  SHL_XOR,
  input  LOGIC_B,
  output Cout,
  output [7:0] Q
);

  wire adder_1_cout, multiplexer_1_out, not_1_out, or_1_out;
  wire [7:0] adder_1_out, bit_extender_1_out, bit_extender_2_out, multiplexer_2_out, multiplexer_3_out,
       multiplexer_5_out, multiplexer_7_out, nor_1_out, xor_1_out, xor_2_out, xor_3_out;
  wire [7:7] and_1_out;

  and and_1 (and_1_out[7], CC, Cin);
  Multiplexer #(.enable("false")) multiplexer_1 (.in0(SUB_AND), .in1(Cin), .out(multiplexer_1_out), .sel(CC));
  not not_1 (not_1_out, SUB_AND);
  Multiplexer #(.width(8), .enable("false")) multiplexer_2 (
    .in0(A), .in1(bit_extender_1_out), .out(multiplexer_2_out), .sel(SHL_XOR));
  assign bit_extender_1_out = {{7{SUB_AND}}, SUB_AND};  // Bit_Extender bit_extender_1
  assign xor_1_out = B ^ multiplexer_2_out;  // XOR_Gate xor_1, 8 bits wide
  assign xor_2_out = A ^ bit_extender_1_out;  // XOR_Gate xor_2, 8 bits wide
  assign bit_extender_2_out = {{7{not_1_out}}, not_1_out};  // Bit_Extender bit_extender_2
  Adder adder_1 (.a(A), .b(xor_1_out), .out(adder_1_out), .cin(multiplexer_1_out), .cout(adder_1_cout));
  assign nor_1_out = ~(xor_1_out | xor_2_out);  // NOR_Gate nor_1, 8 bits wide
  assign xor_3_out = nor_1_out ^ bit_extender_2_out;  // XOR_Gate xor_3, 8 bits wide
  or or_1 (or_1_out, SHL_XOR, not_1_out);
  Multiplexer #(.width(8), .enable("false")) multiplexer_3 (
    .in0(xor_1_out), .in1(xor_3_out), .out(multiplexer_3_out), .sel(SHL_XOR));
  Multiplexer #(.enable("false")) multiplexer_4 (.in0(A[0]), .in1(adder_1_cout), .out(Cout), .sel(or_1_out));
  Multiplexer #(.width(8), .enable("false")) multiplexer_5 (
    .in0({and_1_out[7], A[7:1]}), .in1(B), .out(multiplexer_5_out), .sel(LOGIC_B));
  Multiplexer #(.width(8), .enable("false")) multiplexer_6 (
    .in0(multiplexer_5_out), .in1(multiplexer_7_out), .out(Q), .sel(or_1_out));
  Multiplexer #(.width(8), .enable("false")) multiplexer_7 (
    .in0(adder_1_out), .in1(multiplexer_3_out), .out(multiplexer_7_out), .sel(LOGIC_B));

  // Notes on the sheet:
  //   Cin: pull=down
  //   A: pull=down
  //   B: pull=down
  //   SUB_AND: pull=down
  //   LOGIC_B: pull=down
  //   CC: pull=down
  //   SHL_XOR: pull=down
endmodule
